# Fritzing sketch led_with_resistor (saved by Fritzing 0.9.3b)
breadboards: 1

parts:
  R1 = Resistor [tolerance=±5% resistance=470 package=THT]
  LED1 = LED - 5mm [color="Red (633nm)" package="5 mm [THT]"]
  BAT1 = BC9VPC [package=bc9vpc]

nets:
  N1: R1.Pin_0, LED1.anode
  N2: R1.Pin_1, BAT1.V+
  N3: LED1.cathode, BAT1.V-

notes:
  LED with resistor, The resistor limited the current for the LED. This safe the LED from destroy.
  9 V
  18 mA
  1,6 V
